// Logisim project new_CPU.circ as structural Verilog: 6 circuits, main circuit main
module main (
  output [3:0] out_1,
  output [3:0] out_2,
  output [3:0] out_3,
  output [3:0] out_4,
  output [3:0] out_5,
  output [3:0] out_6,
  output [3:0] out_7,
  output [3:0] out_8,
  output [3:0] out_9,
  output [3:0] out_10,
  output [3:0] out_11,
  output [3:0] out_12,
  output [3:0] out_13,
  output [3:0] out_14,
  output [7:0] out_15
);

  wire Adress, ALU, ALUCarry, ALULogic, and_1_out, and_2_out, and_3_out, and_4_out, and_5_out, Clock,
       decoder_1_out0, decoder_1_out1, demultiplexer_1_out1, Digit, DoJump, FlagWrite, IO_out, Jump,
       not_1_out, not_2_out, w, Write;
  wire [0:0] or_1_out;
  wire [1:0] myalu_1_sign, register_1_q;
  wire [3:0] ALUop, multiplexer_3_out, Operation, Outp, RAMDigit, register_2_q, register_3_q;

  Multiplexer #(.select(2), .width(4)) multiplexer_1 (
    .in0(out_11), .in1(out_11), .in2(RAMDigit), .in3(out_11), .out(out_12), .sel({Adress, or_1_out[0]}));
  TTY #(.cols(33), .rows(5)) tty_1 (.data({out_2[2:0], out_3}), .clk(out_2[3]), .we(1'b1));  // open: clr
  and and_1 (and_1_out, Digit, Adress);
  or or_1 (or_1_out[0], Digit, IO_out);
  Multiplexer #(.width(4)) multiplexer_2 (.in0(out_12), .in1(Outp), .out(out_9), .sel(ALU));
  Registers registers_1 (
    .Data(out_9), .w(w), .t(out_10), .r0(out_1), .r1(out_2), .r2(out_3), .r3(out_4), .r4(out_5), .r5(out_6),
    .r6(out_7), .r7(out_8), .A(out_10), .B(out_11));
  Demultiplexer #(.disabled("Z")) demultiplexer_1 (.out0(w), .out1(demultiplexer_1_out1), .in(Write), .sel(and_1_out));
  Multiplexer #(.disabled("Z"), .width(4)) multiplexer_3 (
    .in0(out_10), .in1(out_11), .out(multiplexer_3_out), .sel(not_1_out));
  not not_1 (not_1_out, Digit);
  RAM #(.addrWidth(4), .dataWidth(4), .enables("line")) ram_1 (
    .addr(multiplexer_3_out), .we(demultiplexer_1_out1), .clk(demultiplexer_1_out1), .din(out_9),
    .dout(RAMDigit));
  MyALU myalu_1 (
    .Cin(ALUCarry), .Operation(ALUop), .A(out_10), .B(out_11), .M(ALULogic), .Outp(Outp),
    .AeqB(myalu_1_sign[1]), .Sign(myalu_1_sign[0]));
  Register #(.width(2)) register_1 (.D(myalu_1_sign), .en(and_2_out), .clk(and_2_out), .Q(register_1_q));  // open: clr
  and and_2 (and_2_out, FlagWrite, not_2_out);
  not not_2 (not_2_out, Clock);
  Clock clock_1 (.out(Clock));
  OperationDecoder operationdecoder_1 (
    .Operation(Operation), .Digit(Digit), .Jump(Jump), .ALULogic(ALULogic), .ALU(ALU), .ALUCarry(ALUCarry),
    .FlagWrite(FlagWrite), .Adress(Adress), .IO_out(IO_out), .ALUop(ALUop));
  nor nor_1 (Write, Clock, Jump);
  Hex_Digit_Display hex_digit_display_1 (.value(Operation));  // open: dp
  Hex_Digit_Display hex_digit_display_2 (.value(out_10));  // open: dp
  Hex_Digit_Display hex_digit_display_3 (.value(out_11));  // open: dp
  JumpHandler jumphandler_1 (
    .a(Operation[0]), .b(Operation[1]), .c(register_1_q[0]), .d(register_1_q[1]), .JumpOp(Jump),
    .DoJump(DoJump));
  PC pc_1 (.Clock(Clock), .DoJump(DoJump), .Operation(Operation), .A_in(out_10), .B_in(out_11));  // open: ClockWait, CA
  Decoder #(.select(4)) decoder_1 (
    .out0(decoder_1_out0), .out1(decoder_1_out1), .sel(out_10), .en(IO_out));  // open: out2, out3, out4, out5, out6, out7, out8, out9, out10, out11, out12, out13, out14, out15
  and and_3 (and_3_out, IO_out, Adress);
  Register #(.width(4)) register_2 (.D(out_9), .clk(and_4_out), .Q(register_2_q));  // open: en, clr
  and and_4 (and_4_out, decoder_1_out0, Write, and_3_out);
  Hex_Digit_Display hex_digit_display_4 (.value(register_2_q));  // open: dp
  Register #(.width(4)) register_3 (.D(out_9), .clk(and_5_out), .Q(register_3_q));  // open: en, clr
  and and_5 (and_5_out, decoder_1_out1, Write, and_3_out);
  Hex_Digit_Display hex_digit_display_5 (.value(register_3_q));  // open: dp

  assign out_13 = out_10;
  assign out_14 = out_11;
  assign out_15 = {out_2, out_3};

  // Other names for the same wires on the sheet: A[3:0] = out_10; A_in[3:0] = out_10; B[3:0] = out_11;
  //   B_in[3:0] = out_11; Data[3:0] = out_9; ID[3:0] = out_12; r0[3:0] = out_1; r3[3:0] = out_4; r4[3:0] = out_5;
  //   r5[3:0] = out_6; r6[3:0] = out_7; r7[3:0] = out_8; r2[3:0] = out_3; ROut[7:0] = {out_2, out_3}; r1[3:0] = out_2

  // Notes on the sheet:
  //   (Eq Bit)(Sign Bit)
endmodule

module MyALU (
  input  Cin,
  input  [3:0] Operation,
  input  [3:0] A,
  input  [3:0] B,
  input  M,
  output [3:0] Outp,
  output AeqB,
  output Sign
);

  wire n74181_1_p13, n74181_1_p14, n74181_1_p16, n74181_1_p18;

  // _74181 74181_1: pin names not known; wires that end beside it: B[0], A[1], A[0], B[1], Operation[3], A[2], Operation[2], B[2], Operation[1], A[3], Operation[0], B[3], n74181_1_p13, n74181_1_p14, M, n74181_1_p16, Outp[0], n74181_1_p18, Outp[1], AeqB, Outp[2], Outp[3]
  nor nor_1 (Sign, n74181_1_p14, AeqB);
  not not_1 (n74181_1_p13, Cin);

  // Notes on the sheet:
  //   Cout
  //   Pn
endmodule

module Registers (
  input  [3:0] Data,
  input  w,
  input  [3:0] t,
  output [3:0] r0,
  output [3:0] r1,
  output [3:0] r2,
  output [3:0] r3,
  output [3:0] r4,
  output [3:0] r5,
  output [3:0] r6,
  output [3:0] r7,
  output [3:0] A,
  output [3:0] B
);

  wire r0_w, r1_w, r2_w, r3_w, r4_w, r5_w, r6_w, r7_w;
  wire [2:0] A_t, B_t;

  Register #(.width(4)) register_1 (.D(Data), .clk(r0_w), .Q(r0));  // open: en, clr
  Register #(.width(4)) register_2 (.D(Data), .clk(r1_w), .Q(r1));  // open: en, clr
  Register #(.width(4)) register_3 (.D(Data), .clk(r2_w), .Q(r2));  // open: en, clr
  Register #(.width(4)) register_4 (.D(Data), .clk(r3_w), .Q(r3));  // open: en, clr
  Register #(.width(4)) register_5 (.D(Data), .clk(r4_w), .Q(r4));  // open: en, clr
  Register #(.width(4)) register_6 (.D(Data), .clk(r5_w), .Q(r5));  // open: en, clr
  Register #(.width(4)) register_7 (.D(Data), .clk(r6_w), .Q(r6));  // open: en, clr
  Register #(.width(4)) register_8 (.D(Data), .clk(r7_w), .Q(r7));  // open: en, clr
  Demultiplexer #(.select(3)) demultiplexer_1 (
    .out0(r0_w), .out1(r1_w), .out2(r2_w), .out3(r3_w), .out4(r4_w), .out5(r5_w), .out6(r6_w), .out7(r7_w),
    .in(w), .sel(t[2:0]));
  Multiplexer #(.select(3), .width(4)) multiplexer_1 (
    .in0(r0), .in1(r1), .in2(r2), .in3(r3), .in4(r4), .in5(r5), .in6(r6), .in7(r7), .out(A), .sel(A_t));
  Multiplexer #(.select(3), .width(4)) multiplexer_2 (
    .in0(r0), .in1(r1), .in2(r2), .in3(r3), .in4(r4), .in5(r5), .in6(r6), .in7(r7), .out(B), .sel(B_t));
endmodule

module PC (
  input  Clock,
  input  DoJump,
  input  ClockWait,
  output [7:0] CA,
  output [3:0] Operation,
  output [3:0] A_in,
  output [3:0] B_in
);

  wire ClockUpd, not_1_out;
  wire [7:0] controlled_buffer_1_out, counter_1_q;

  Counter #(.ongoal("stay")) counter_1 (
    .load(DoJump), .clk(ClockUpd), .D({A_in, B_in}), .Q(counter_1_q));  // open: clr, up, count, carry
  assign controlled_buffer_1_out = not_1_out ? counter_1_q : 8'bz;  // Controlled_Buffer controlled_buffer_1
  ROM #(.dataWidth(12)) rom_1 (.addr(controlled_buffer_1_out), .data({Operation, A_in, B_in}));
  not not_1 (not_1_out, ClockWait);
  and and_1 (ClockUpd, not_1_out, Clock);
  // AND_Gate and_2 has open pins: in2=DoJump, out=open

  assign CA = {A_in, B_in};

  // Other names for the same wires on the sheet: CurrAdress[7:0] = {A_in, B_in}

  // Notes on the sheet:
  //   contents of rom_1 (hex, n*v repeats v):
  //   0 100 111 124 135 b02 b13
endmodule

module OperationDecoder (
  input  [3:0] Operation,
  output Digit,
  output Jump,
  output ALULogic,
  output ALU,
  output ALUCarry,
  output FlagWrite,
  output Adress,
  output IO_out,
  output [3:0] ALUop
);

  wire [15:8] rom_1_data;

  ROM #(.addrWidth(4), .dataWidth(16)) rom_1 (
    .addr(Operation), .data({rom_1_data, IO_out, Adress, FlagWrite, ALUCarry, ALU, ALULogic, Jump, Digit}));

  assign ALUop = Operation;

  // Notes on the sheet:
  //   contents of rom_1 (hex, n*v repeats v):
  //   0 1 41 40 c 0 38 0 0 8 0 c0 4*2
endmodule

module JumpHandler (
  input  a,
  input  b,
  input  c,
  input  d,
  input  JumpOp,
  output DoJump
);

  wire and_1_out, and_2_out, and_3_out, and_4_out, or_1_out;

  and and_1 (and_1_out, a, b, ~c);  // AND_Gate
  and and_2 (and_2_out, ~b, c);  // AND_Gate
  and and_3 (and_3_out, ~a, b, d);  // AND_Gate
  and and_4 (and_4_out, a, ~b, d);  // AND_Gate
  and and_5 (DoJump, or_1_out, JumpOp);
  or or_1 (or_1_out, and_1_out, and_2_out, and_3_out, and_4_out);
endmodule
