// Logisim project main.circ as structural Verilog: 13 circuits, main circuit Main
module Main (
);

  wire button_1_out, clock_1_out, clock_2_out, cpu_1_mr, cpu_1_mw, cpu_1_nothalt, dipswitch_1_sw1,
       dipswitch_1_sw2;
  wire [7:0] cpu_1_dataout, ram_1_dout;
  wire [15:0] cpu_1_address;

  Clock #(.highDuration(2), .lowDuration(2)) clock_1 (.out(clock_1_out));
  DipSwitch #(.number(2)) dipswitch_1 (.sw1(dipswitch_1_sw1), .sw2(dipswitch_1_sw2));
  Button button_1 (.out(button_1_out));
  Clock clock_2 (.out(clock_2_out));
  CPU cpu_1 (
    .DataIn(ram_1_dout), .Clk(clock_1_out), .NotReset(dipswitch_1_sw1), .NotWait(dipswitch_1_sw2),
    .Irq(button_1_out), .DataOut(cpu_1_dataout), .NotHalt(cpu_1_nothalt), .MR(cpu_1_mr), .MW(cpu_1_mw),
    .Address(cpu_1_address));  // open: IntAck
  LED led_1 (.in(cpu_1_nothalt));
  RAM #(.addrWidth(16)) ram_1 (
    .addr(cpu_1_address), .we(cpu_1_mw), .oe(cpu_1_mr), .clk(clock_2_out), .din(cpu_1_dataout),
    .dout(ram_1_dout));
endmodule

module StackPointer (
  input  NotReset,
  input  HFromD,
  input  Clk,
  input  HToD,
  input  [7:0] DIn,
  input  LFromD,
  input  NotInc,
  input  LToD,
  input  NotDec,
  output [7:0] DOut
);

  wire and_1_out, counter_2_carry, not_1_out, not_2_out, not_3_out, or_1_out;
  wire [3:0] counter_1_q, counter_1_q_2, counter_2_q, counter_2_q_2;

  not not_1 (not_1_out, NotReset);
  not not_2 (not_2_out, NotInc);
  not not_3 (not_3_out, NotDec);
  or or_1 (or_1_out, not_2_out, not_3_out);
  Counter counter_1 (
    .clr(not_1_out), .load(HFromD), .up(not_2_out), .count(and_1_out), .clk(Clk), .D(DIn),
    .Q({counter_1_q_2, counter_1_q}));  // open: carry
  and and_1 (and_1_out, or_1_out, counter_2_carry);
  Counter counter_2 (
    .clr(not_1_out), .load(LFromD), .up(not_2_out), .count(or_1_out), .clk(Clk), .D(DIn),
    .carry(counter_2_carry), .Q({counter_2_q_2, counter_2_q}));
  assign DOut = HToD ? {counter_1_q_2, counter_1_q} : 8'bz;  // Controlled_Buffer controlled_buffer_1
  assign DOut = LToD ? {counter_2_q_2, counter_2_q} : 8'bz;  // Controlled_Buffer controlled_buffer_2
  Hex_Digit_Display hex_digit_display_1 (.value(counter_1_q_2));  // open: dp
  Hex_Digit_Display hex_digit_display_2 (.value(counter_1_q));  // open: dp
  Hex_Digit_Display hex_digit_display_3 (.value(counter_2_q_2));  // open: dp
  Hex_Digit_Display hex_digit_display_4 (.value(counter_2_q));  // open: dp
endmodule

module CPU (
  input  [7:0] DataIn,
  input  Clk,
  input  NotReset,
  input  NotWait,
  input  Irq,
  output [7:0] DataOut,
  output IntAck,
  output NotHalt,
  output MR,
  output MW,
  output [15:0] Address
);

  wire AccFromD, AccShLeft, AccShRight, AccToD, AddrHFromD, AddrLFromD, ALUCarry, ALUEnable, ALUMode,
       CnstToD, FRFromD, FRToD, FRUpdate, IRFromD, NotAddrDec, NotAddrInc, NotPCInc, NotSPDec, NotSPInc,
       or_1_out, PCHFromD, PCHToD, PCLFromD, PCLToD, SCClear, SPHFromD, SPHToD, SPLFromD, SPLToD, TmpHFromD,
       TmpHToD, TmpLFromD, TmpLToD;
  wire [2:0] alu_1_flagsout, Flags;
  wire [3:0] ALUSel, Step;
  wire [4:0] FromD, ToD;
  wire [7:0] Accum, argumentregister_1_hout, DBus, Instruction;

  LedBar #(.matrixcols(3)) ledbar_1 (.led0(Flags[0]), .led1(Flags[1]), .led2(Flags[2]));
  Hex_Digit_Display hex_digit_display_1 (.value(Step));  // open: dp
  Hex_Digit_Display hex_digit_display_2 (.value(Accum[7:4]));  // open: dp
  Hex_Digit_Display hex_digit_display_3 (.value(Accum[3:0]));  // open: dp
  Hex_Digit_Display hex_digit_display_4 (.value(Instruction[7:4]));  // open: dp
  StackPointer stackpointer_1 (
    .NotReset(NotReset), .HFromD(SPHFromD), .Clk(Clk), .HToD(SPHToD), .DIn(DBus), .LFromD(SPLFromD),
    .NotInc(NotSPInc), .LToD(SPLToD), .NotDec(NotSPDec), .DOut(DBus));
  Hex_Digit_Display hex_digit_display_5 (.value(Instruction[3:0]));  // open: dp
  Hex_Digit_Display hex_digit_display_6 (.value(DBus[7:4]));  // open: dp
  Hex_Digit_Display hex_digit_display_7 (.value(DBus[3:0]));  // open: dp
  RegisterFile registerfile_1 (.DIn(DBus), .FromD(FromD), .ToD(ToD), .NotReset(NotReset), .Clk(Clk), .DOut(DBus));
  ProgramCounter programcounter_1 (
    .NotReset(NotReset), .HFromD(PCHFromD), .Clk(Clk), .HToD(PCHToD), .DIn(DBus), .LFromD(PCLFromD),
    .NotInc(NotPCInc), .LToD(PCLToD), .DOut(DBus));
  InstructionRegister instructionregister_1 (
    .DIn(DBus), .FromD(IRFromD), .Clk(Clk), .NotReset(NotReset), .Instruction(Instruction));
  Accumulator accumulator_1 (
    .DIn(DBus), .FromD(AccFromD), .ShiftLeft(AccShLeft), .ShiftRight(AccShRight), .Clk(Clk),
    .NotReset(NotReset), .ToD(AccToD), .ALUOut(Accum), .DOut(DBus));
  ArgumentRegister argumentregister_1 (
    .HToD(TmpHToD), .LToD(TmpLToD), .NotReset(NotReset), .HFromD(TmpHFromD), .Clk(Clk), .DIn(DBus),
    .LFromD(TmpLFromD), .DOut(DBus), .HOut(argumentregister_1_hout));
  assign DBus = CnstToD ? 8'h1c : 8'bz;  // Controlled_Buffer controlled_buffer_1
  ALU alu_1 (
    .DIn(Accum), .Enable(ALUEnable), .AccIn(argumentregister_1_hout), .Sel(ALUSel), .Carry(ALUCarry),
    .Mode(ALUMode), .DOut(DBus), .FlagsOut(alu_1_flagsout));
  AddressRegister addressregister_1 (
    .NotReset(NotReset), .HFromD(AddrHFromD), .Clk(Clk), .DIn(DBus), .LFromD(AddrLFromD),
    .NotInc(NotAddrInc), .NotDec(NotAddrDec), .Address(Address));
  or or_1 (or_1_out, IntAck, MR);
  assign DBus = or_1_out ? DataIn : 8'bz;  // Controlled_Buffer controlled_buffer_2
  assign DataOut = MW ? DBus : 8'bz;  // Controlled_Buffer controlled_buffer_3
  FlagRegister flagregister_1 (
    .FlagsIn(alu_1_flagsout), .DIn(DBus), .FromD(FRFromD), .Update(FRUpdate), .ToD(FRToD), .Clk(Clk),
    .NotReset(NotReset), .FlagsOut(Flags), .DOut(DBus));
  StepCounter stepcounter_1 (
    .Clk(Clk), .NotReset(NotReset), .Clear(SCClear), .NotHalt(NotHalt), .NotWait(NotWait), .Step(Step));
  InstructionDecoder instructiondecoder_1 (
    .Clk(Clk), .IntReq(Irq), .Instruction(Instruction), .Flags(Flags), .Step(Step), .MemFromD(MW),
    .SPHFromD(SPHFromD), .SPLFromD(SPLFromD), .PCHFromD(PCHFromD), .PCLFromD(PCLFromD),
    .TmpHFromD(TmpHFromD), .TmpLFromD(TmpLFromD), .AccFromD(AccFromD), .FRFromD(FRFromD), .IRFromD(IRFromD),
    .AddrHFromD(AddrHFromD), .AddrLFromD(AddrLFromD), .FromD(FromD), .ALUMode(ALUMode), .MemToD(MR),
    .ALUCarry(ALUCarry), .SPHToD(SPHToD), .FRUpdate(FRUpdate), .SPLToD(SPLToD), .PCHToD(PCHToD),
    .PCLToD(PCLToD), .TmpHToD(TmpHToD), .TmpLToD(TmpLToD), .AccToD(AccToD), .FRToD(FRToD), .CnstToD(CnstToD),
    .ALUEnable(ALUEnable), .SCClear(SCClear), .IntAck(IntAck), .NotHalt(NotHalt), .NotPCInc(NotPCInc),
    .ToD(ToD), .ALUSel(ALUSel), .NotSPDec(NotSPDec), .NotSPInc(NotSPInc), .AccShLeft(AccShLeft),
    .AccShRight(AccShRight), .NotAddrDec(NotAddrDec), .NotAddrInc(NotAddrInc));

  // Other names for the same wires on the sheet: IntReq = Irq; MemFromD = MW; MemToD = MR
endmodule

module ArgumentRegister (
  input  HToD,
  input  LToD,
  input  NotReset,
  input  HFromD,
  input  Clk,
  input  [7:0] DIn,
  input  LFromD,
  output [7:0] DOut,
  output [7:0] HOut
);

  wire n74273_1_pin11, n74273_2_pin11;
  wire [3:0] n74273_2_pin2, n74273_2_pin12;

  _74273 u_74273_1 (
    .pin1(NotReset), .pin2(HOut[0]), .pin3(DIn[0]), .pin4(DIn[1]), .pin5(HOut[1]), .pin6(HOut[2]),
    .pin7(DIn[2]), .pin8(DIn[3]), .pin9(HOut[3]), .pin19(HOut[7]), .pin18(DIn[7]), .pin17(DIn[6]),
    .pin16(HOut[6]), .pin15(HOut[5]), .pin14(DIn[5]), .pin13(DIn[4]), .pin12(HOut[4]), .pin11(n74273_1_pin11));
  and and_1 (n74273_1_pin11, HFromD, Clk);
  _74273 u_74273_2 (
    .pin1(NotReset), .pin2(n74273_2_pin2[0]), .pin3(DIn[0]), .pin4(DIn[1]), .pin5(n74273_2_pin2[1]),
    .pin6(n74273_2_pin2[2]), .pin7(DIn[2]), .pin8(DIn[3]), .pin9(n74273_2_pin2[3]),
    .pin19(n74273_2_pin12[3]), .pin18(DIn[7]), .pin17(DIn[6]), .pin16(n74273_2_pin12[2]),
    .pin15(n74273_2_pin12[1]), .pin14(DIn[5]), .pin13(DIn[4]), .pin12(n74273_2_pin12[0]),
    .pin11(n74273_2_pin11));
  assign DOut = HToD ? HOut : 8'bz;  // Controlled_Buffer controlled_buffer_1
  and and_2 (n74273_2_pin11, LFromD, Clk);
  assign DOut = LToD ? {n74273_2_pin12, n74273_2_pin2} : 8'bz;  // Controlled_Buffer controlled_buffer_2
  Hex_Digit_Display hex_digit_display_1 (.value(HOut[7:4]));  // open: dp
  Hex_Digit_Display hex_digit_display_2 (.value(HOut[3:0]));  // open: dp
  Hex_Digit_Display hex_digit_display_3 (.value(n74273_2_pin12));  // open: dp
  Hex_Digit_Display hex_digit_display_4 (.value(n74273_2_pin2));  // open: dp
endmodule

module Accumulator (
  input  [7:0] DIn,
  input  FromD,
  input  ShiftLeft,
  input  ShiftRight,
  input  Clk,
  input  NotReset,
  input  ToD,
  output [7:0] ALUOut,
  output [7:0] DOut
);

  wire and_1_out, and_2_out, and_3_out, nor_1_out, not_1_out;

  Register register_1 (.D(DIn), .en(FromD), .clk(Clk), .Q(ALUOut), .clr(not_1_out));
  not not_1 (not_1_out, NotReset);
  and and_1 (and_1_out, ShiftLeft, ToD);
  assign DOut = and_3_out ? {1'b0, ALUOut[7:1]} : 8'bz;  // Controlled_Buffer controlled_buffer_1
  assign DOut = and_1_out ? {ALUOut[6:0], 1'b0} : 8'bz;  // Controlled_Buffer controlled_buffer_2
  assign DOut = and_2_out ? ALUOut : 8'bz;  // Controlled_Buffer controlled_buffer_3
  and and_2 (and_2_out, ToD, nor_1_out);
  nor nor_1 (nor_1_out, ShiftLeft, ShiftRight);
  and and_3 (and_3_out, ShiftRight, ToD);
endmodule

module ALU (
  input  [7:0] DIn,
  input  Enable,
  input  [7:0] AccIn,
  input  [3:0] Sel,
  input  Carry,
  input  Mode,
  output [7:0] DOut,
  output [2:0] FlagsOut
);

  wire n74181_1_p13, NotCarry, Sign, Zero;
  wire [6:0] n74181_2_p17;

  // _74181 74181_1: pin names not known; wires that end beside it: AccIn[4], DIn[5], DIn[4], AccIn[5], Sel[3], DIn[6], Sel[2], AccIn[6], Sel[1], DIn[7], Sel[0], AccIn[7], n74181_1_p13, Mode, NotCarry, n74181_2_p17[4], n74181_2_p17[5], Sign
  // _74181 74181_2: pin names not known; wires that end beside it: n74181_2_p17[6], AccIn[0], DIn[1], DIn[0], AccIn[1], Sel[3], DIn[2], Sel[2], AccIn[2], Sel[1], DIn[3], Sel[0], AccIn[3], Carry, Mode, n74181_1_p13, n74181_2_p17[0], n74181_2_p17[1], n74181_2_p17[2], n74181_2_p17[3]
  nor nor_1 (Zero, Sign, n74181_2_p17[6], n74181_2_p17[5], n74181_2_p17[4], n74181_2_p17[2], n74181_2_p17[0], n74181_2_p17[1], n74181_2_p17[3]);
  assign DOut = Enable ? {Sign, n74181_2_p17} : 8'bz;  // Controlled_Buffer controlled_buffer_1
  assign FlagsOut = Enable ? {Zero, NotCarry, Sign} : 3'bz;  // Controlled_Buffer controlled_buffer_2
endmodule

module FlagRegister (
  input  [2:0] FlagsIn,
  input  [7:0] DIn,
  input  FromD,
  input  Update,
  input  ToD,
  input  Clk,
  input  NotReset,
  output [2:0] FlagsOut,
  output [7:0] DOut
);

  wire not_1_out, or_1_out;
  wire [4:0] controlled_buffer_1_out;
  wire [7:3] register_1_q;

  assign {controlled_buffer_1_out, FlagsIn} = FromD ? DIn : 8'bz;  // Controlled_Buffer controlled_buffer_1
  or or_1 (or_1_out, FromD, Update);
  Register register_1 (
    .D({controlled_buffer_1_out, FlagsIn}), .en(or_1_out), .clk(Clk), .Q({register_1_q, FlagsOut}),
    .clr(not_1_out));
  not not_1 (not_1_out, NotReset);
  assign DOut = ToD ? {register_1_q, FlagsOut} : 8'bz;  // Controlled_Buffer controlled_buffer_2
  // also tied to GND on the sheet: {controlled_buffer_1_out[0], controlled_buffer_1_out[1], controlled_buffer_1_out[2], controlled_buffer_1_out[3], controlled_buffer_1_out[4]}
endmodule

module InstructionRegister (
  input  [7:0] DIn,
  input  FromD,
  input  Clk,
  input  NotReset,
  output [7:0] Instruction
);

  wire not_1_out;

  Register register_1 (.D(DIn), .en(FromD), .clk(Clk), .Q(Instruction), .clr(not_1_out));
  not not_1 (not_1_out, NotReset);
endmodule

module RegisterFile (
  input  [7:0] DIn,
  input  [4:0] FromD,
  input  [4:0] ToD,
  input  NotReset,
  input  Clk,
  output [7:0] DOut
);

  wire decoder_1_out9, decoder_1_out10, decoder_1_out11, decoder_1_out12, decoder_1_out13, not_1_out;
  wire [7:0] register_1_q, register_2_q, register_3_q, register_4_q, register_5_q;

  Decoder #(.select(5)) decoder_1 (
    .out9(decoder_1_out9), .out10(decoder_1_out10), .out11(decoder_1_out11), .out12(decoder_1_out12),
    .out13(decoder_1_out13), .sel(FromD));  // open: out0, out1, out2, out3, out4, out5, out6, out7, out8, out14, out15, out16, out17, out18, out19, out20, out21, out22, out23, out24, out25, out26, out27, out28, out29, out30, out31, en
  not not_1 (not_1_out, NotReset);
  Register register_1 (.D(DIn), .en(decoder_1_out9), .clk(Clk), .Q(register_1_q), .clr(not_1_out));
  Register register_2 (.D(DIn), .en(decoder_1_out10), .clk(Clk), .Q(register_2_q), .clr(not_1_out));
  Register register_3 (.D(DIn), .en(decoder_1_out11), .clk(Clk), .Q(register_3_q), .clr(not_1_out));
  Register register_4 (.D(DIn), .en(decoder_1_out12), .clk(Clk), .Q(register_4_q), .clr(not_1_out));
  Register register_5 (.D(DIn), .en(decoder_1_out13), .clk(Clk), .Q(register_5_q), .clr(not_1_out));
  Multiplexer #(.enable("true"), .select(5), .width(8)) multiplexer_1 (
    .in9(register_1_q), .in10(register_2_q), .in11(register_3_q), .in12(register_4_q), .in13(register_5_q),
    .out(DOut), .sel(ToD));  // open: in0, in1, in2, in3, in4, in5, in6, in7, in8, in14, in15, in16, in17, in18, in19, in20, in21, in22, in23, in24, in25, in26, in27, in28, in29, in30, in31, en
endmodule

module InstructionDecoder (
  input  Clk,
  input  IntReq,
  input  [7:0] Instruction,
  input  [2:0] Flags,
  input  [3:0] Step,
  output MemFromD,
  output SPHFromD,
  output SPLFromD,
  output PCHFromD,
  output PCLFromD,
  output TmpHFromD,
  output TmpLFromD,
  output AccFromD,
  output FRFromD,
  output IRFromD,
  output AddrHFromD,
  output AddrLFromD,
  output [4:0] FromD,
  output ALUMode,
  output MemToD,
  output ALUCarry,
  output SPHToD,
  output FRUpdate,
  output SPLToD,
  output PCHToD,
  output PCLToD,
  output TmpHToD,
  output TmpLToD,
  output AccToD,
  output FRToD,
  output CnstToD,
  output ALUEnable,
  output SCClear,
  output IntAck,
  output NotHalt,
  output NotPCInc,
  output [4:0] ToD,
  output [3:0] ALUSel,
  output NotSPDec,
  output NotSPInc,
  output AccShLeft,
  output AccShRight,
  output NotAddrDec,
  output NotAddrInc
);

  wire IntDisable, IntEnable, j_k_ff_1_q, j_k_ff_1_qn;
  wire [7:4] rom_4_data;
  wire [15:15] and_1_out;

  and and_1 (and_1_out[15], 1'b1, j_k_ff_1_qn);
  J_K_Flip_Flop j_k_ff_1 (
    .J(IntDisable), .K(IntEnable), .clk(Clk), .Q(j_k_ff_1_q), .Qn(j_k_ff_1_qn));  // open: preset, reset
  ROM #(.addrWidth(16)) rom_1 (
    .addr({and_1_out[15], Step, Flags, Instruction}), .data({FRUpdate, ALUCarry, ALUMode, FromD}));
  ROM #(.addrWidth(16)) rom_2 (
    .addr({and_1_out[15], Step, Flags, Instruction}), .data({NotPCInc, NotHalt, SCClear, ToD}));
  ROM #(.addrWidth(16)) rom_3 (
    .addr({and_1_out[15], Step, Flags, Instruction}),
    .data({AccShRight, AccShLeft, NotSPInc, NotSPDec, ALUSel}));
  ROM #(.addrWidth(16)) rom_4 (
    .addr({and_1_out[15], Step, Flags, Instruction}),
    .data({rom_4_data, NotAddrInc, NotAddrDec, IntDisable, IntEnable}));
  Decoder #(.select(5)) decoder_1 (
    .out1(MemFromD), .out2(SPHFromD), .out3(SPLFromD), .out4(PCHFromD), .out5(PCLFromD), .out6(TmpHFromD),
    .out7(TmpLFromD), .out8(AccFromD), .out14(FRFromD), .out15(IRFromD), .out16(AddrHFromD),
    .out17(AddrLFromD), .sel(FromD));  // open: out0, out9, out10, out11, out12, out13, out18, out19, out20, out21, out22, out23, out24, out25, out26, out27, out28, out29, out30, out31, en
  Decoder #(.select(5)) decoder_2 (
    .out1(MemToD), .out2(SPHToD), .out3(SPLToD), .out4(PCHToD), .out5(PCLToD), .out6(TmpHToD),
    .out7(TmpLToD), .out8(AccToD), .out14(FRToD), .out15(CnstToD), .out16(ALUEnable), .out17(IntAck),
    .sel(ToD));  // open: out0, out9, out10, out11, out12, out13, out18, out19, out20, out21, out22, out23, out24, out25, out26, out27, out28, out29, out30, out31, en

  // Other names for the same wires on the sheet: FromDBus[4:0] = FromD; ToDBus[4:0] = ToD

  // Notes on the sheet:
  //   contents of rom_1 (hex, n*v repeats v):
  //   50 40 40 36*50 49 4a 4b 4e 4c 4d 48 4a 4b 4e 4c 4d 48 49 4b 4e 4c 4d 48 49 4a 4e 4c 4d 48 49 4a 4b
  //   4c 4d 48 49 4a 4b 4e 4d 48 49 4a 4b 4e 4c 42 4d 4d 11*50 10*40 50 44 5*50 44 50 44 50 50 50 44 7*50
  //   40 50 50 40 40 50 40 6*46 50 6*46 50 6*46 50 6*46 50 6*46 50 6*46 50 6*46 50 6*46 50 36*46 50 48 48
  //   40 27*0 50 40 40 36*50 49 4a 4b 4e 4c 4d 48 4a 4b 4e 4c 4d 48 49 4b 4e 4c 4d 48 49 4a 4e 4c 4d 48 49
  //   4a 4b 4c 4d 48 49 4a 4b 4e 4d 48 49 4a 4b 4e 4c 42 4d 4d 11*50 10*40 50 44 5*50 44 50 50 50 44 50 44
  //   7*50 40 50 50 40 50 40 40 6*46 50 6*46 50 6*46 50 6*46 50 6*46 50 6*46 50 6*46 50 6*46 50 36*46 50
  //   48 48 40 27*0 50 40 40 36*50 49 4a 4b 4e 4c 4d 48 4a 4b 4e 4c 4d 48 49 4b 4e 4c 4d 48 49 4a 4e 4c 4d
  //   48 49 4a 4b 4c 4d 48 49 4a 4b 4e 4d 48 49 4a 4b 4e 4c 42 4d 4d 11*50 10*40 50 44 50 50 50 44 50 50
  //   50 44 50 50 50 44 7*50 40 50 40 50 40 50 40 6*46 50 6*46 50 6*46 50 6*46 50 6*46 50 6*46 50 6*46 50
  //   6*46 50 36*46 50 48 48 40 27*0 50 40 40 36*50 49 4a 4b 4e 4c 4d 48 4a 4b 4e 4c 4d 48 49 4b 4e 4c 4d
  //   48 49 4a 4e 4c 4d 48 49 4a 4b 4c 4d 48 49 4a 4b 4e 4d 48 49 4a 4b 4e 4c 42 4d 4d 11*50 10*40 50 44
  //   50 50 50 44 5*50 44 50 44 7*50 40 50 40 50 50 40 40 6*46 50 6*46 50 6*46 50 6*46 50 6*46 50 6*46 50
  //   6*46 50 6*46 50 36*46 50 48 48 40 27*0 50 40 40 36*50 49 4a 4b 4e 4c 4d 48 4a 4b 4e 4c 4d 48 49 4b
  //   4e 4c 4d 48 49 4a 4e 4c 4d 48 49 4a 4b 4c 4d 48 49 4a 4b 4e 4d 48 49 4a 4b 4e 4c 42 4d 4d 11*50
  //   10*40 50 50 50 44 50 50 50 44 50 44 50 50 50 44 8*50 40 50 40 40 50 40 6*46 50 6*46 50 6*46 50 6*46
  //   50 6*46 50 6*46 50 6*46 50 6*46 50 36*46 50 48 48 40 27*0 50 40 40 36*50 49 4a 4b 4e 4c 4d 48 4a 4b
  //   4e 4c 4d 48 49 4b 4e 4c 4d 48 49 4a 4e 4c 4d 48 49 4a 4b 4c 4d 48 49 4a 4b 4e 4d 48 49 4a 4b 4e 4c
  //   42 4d 4d 11*50 10*40 50 50 50 44 50 50 50 44 50 50 50 44 50 44 8*50 40 50 40 50 40 40 6*46 50 6*46
  //   50 6*46 50 6*46 50 6*46 50 6*46 50 6*46 50 6*46 50 36*46 50 48 48 40 27*0 50 40 40 36*50 49 4a 4b 4e
  //   4c 4d 48 4a 4b 4e 4c 4d 48 49 4b 4e 4c 4d 48 49 4a 4e 4c 4d 48 49 4a 4b 4c 4d 48 49 4a 4b 4e 4d 48
  //   49 4a 4b 4e 4c 42 4d 4d 11*50 10*40 50 50 50 44 50 44 50 50 50 44 50 50 50 44 8*50 40 40 50 40 50 40
  //   6*46 50 6*46 50 6*46 50 6*46 50 6*46 50 6*46 50 6*46 50 6*46 50 36*46 50 48 48 40 27*0 50 40 40
  //   36*50 49 4a 4b 4e 4c 4d 48 4a 4b 4e 4c 4d 48 49 4b 4e 4c 4d 48 49 4a 4e 4c 4d 48 49 4a 4b 4c 4d 48
  //   49 4a 4b 4e 4d 48 49 4a 4b 4e 4c 42 4d 4d 11*50 10*40 50 50 50 44 50 44 5*50 44 50 44 8*50 40 40 50
  //   50 40 40 6*46 50 6*46 50 6*46 50 6*46 50 6*46 50 6*46 50 6*46 50 6*46 50 36*46 50 48 48 40 27*0 51
  //   50 50 36*51 42*50 43 4c 4c 11*51 10*50 51 45 5*51 45 51 45 51 51 51 45 7*51 50 51 51 50 50 51 50
  //   6*c8 51 6*c8 51 6*e8 51 6*e8 51 6*e8 51 6*e8 51 6*88 51 6*88 51 88 89 8a 8b 8c 8d c8 c9 ca cb cc cd
  //   88 89 8a 8b 8c 8d c8 c9 ca cb cc cd e8 e9 ea eb ec ed 6*c0 51 50 50 28*0 51 50 50 36*51 42*50 43 4c
  //   4c 11*51 10*50 51 45 5*51 45 51 51 51 45 51 45 7*51 50 51 51 50 51 50 50 6*c8 51 6*c8 51 6*e8 51
  //   6*e8 51 6*e8 51 6*e8 51 6*88 51 6*88 51 88 89 8a 8b 8c 8d c8 c9 ca cb cc cd 88 89 8a 8b 8c 8d c8 c9
  //   ca cb cc cd e8 e9 ea eb ec ed 6*c0 51 50 50 28*0 51 50 50 36*51 42*50 43 4c 4c 11*51 10*50 51 45 51
  //   51 51 45 51 51 51 45 51 51 51 45 7*51 50 51 50 51 50 51 50 6*c8 51 6*c8 51 6*e8 51 6*e8 51 6*e8 51
  //   6*e8 51 6*c8 51 6*c8 51 88 89 8a 8b 8c 8d c8 c9 ca cb cc cd c8 c9 ca cb cc cd 88 89 8a 8b 8c 8d e8
  //   e9 ea eb ec ed 6*c0 51 50 50 28*0 51 50 50 36*51 42*50 43 4c 4c 11*51 10*50 51 45 51 51 51 45 5*51
  //   45 51 45 7*51 50 51 50 51 51 50 50 6*c8 51 6*c8 51 6*e8 51 6*e8 51 6*e8 51 6*e8 51 6*c8 51 6*c8 51
  //   88 89 8a 8b 8c 8d c8 c9 ca cb cc cd c8 c9 ca cb cc cd 88 89 8a 8b 8c 8d e8 e9 ea eb ec ed 6*c0 51 50
  //   50 28*0 51 50 50 36*51 42*50 43 4c 4c 11*51 10*50 51 51 51 45 51 51 51 45 51 45 51 51 51 45 8*51 50
  //   51 50 50 51 50 6*c8 51 6*c8 51 6*e8 51 6*e8 51 6*e8 51 6*e8 51 6*88 51 6*88 51 88 89 8a 8b 8c 8d c8
  //   c9 ca cb cc cd 88 89 8a 8b 8c 8d c8 c9 ca cb cc cd e8 e9 ea eb ec ed 6*c0 51 50 50 28*0 51 50 50
  //   36*51 42*50 43 4c 4c 11*51 10*50 51 51 51 45 51 51 51 45 51 51 51 45 51 45 8*51 50 51 50 51 50 50
  //   6*c8 51 6*c8 51 6*e8 51 6*e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
  //   contents of rom_2 (hex, n*v repeats v):
  //   c4 c0 c0 18*c4 5*cd c4 c4 c2 5*c4 5*cd 6*c8 6*c9 6*ca 6*cb 6*ce 6*cc 7*cd c2 c4 11*c2 10*c0 c4 cd
  //   5*c4 cd c4 cd c4 c4 c4 cd 7*c4 c0 c4 c4 c0 c0 c4 c0 c8 c9 ca cb cc cd c4 c8 c9 ca cb cc cd c4 c8 c9
  //   ca cb cc cd c4 c8 c9 ca cb cc cd c4 c8 c9 ca cb cc cd c4 c8 c9 ca cb cc cd c4 c8 c9 ca cb cc cd c4
  //   c8 c9 ca cb cc cd c4 c8 c9 ca cb cc cd c8 c9 ca cb cc cd c8 c9 ca cb cc cd c8 c9 ca cb cc cd c8 c9
  //   ca cb cc cd c8 c9 ca cb cc cd c4 c8 c8 80 27*0 c4 c0 c0 18*c4 5*cd c4 c4 c2 5*c4 5*cd 6*c8 6*c9 6*ca
  //   6*cb 6*ce 6*cc 7*cd c2 c4 11*c2 10*c0 c4 cd 5*c4 cd c4 c4 c4 cd c4 cd 7*c4 c0 c4 c4 c0 c4 c0 c0 c8
  //   c9 ca cb cc cd c4 c8 c9 ca cb cc cd c4 c8 c9 ca cb cc cd c4 c8 c9 ca cb cc cd c4 c8 c9 ca cb cc cd
  //   c4 c8 c9 ca cb cc cd c4 c8 c9 ca cb cc cd c4 c8 c9 ca cb cc cd c4 c8 c9 ca cb cc cd c8 c9 ca cb cc
  //   cd c8 c9 ca cb cc cd c8 c9 ca cb cc cd c8 c9 ca cb cc cd c8 c9 ca cb cc cd c4 c8 c8 80 27*0 c4 c0 c0
  //   18*c4 5*cd c4 c4 c2 5*c4 5*cd 6*c8 6*c9 6*ca 6*cb 6*ce 6*cc 7*cd c2 c4 11*c2 10*c0 c4 cd c4 c4 c4 cd
  //   c4 c4 c4 cd c4 c4 c4 cd 7*c4 c0 c4 c0 c4 c0 c4 c0 c8 c9 ca cb cc cd c4 c8 c9 ca cb cc cd c4 c8 c9 ca
  //   cb cc cd c4 c8 c9 ca cb cc cd c4 c8 c9 ca cb cc cd c4 c8 c9 ca cb cc cd c4 c8 c9 ca cb cc cd c4 c8
  //   c9 ca cb cc cd c4 c8 c9 ca cb cc cd c8 c9 ca cb cc cd c8 c9 ca cb cc cd c8 c9 ca cb cc cd c8 c9 ca
  //   cb cc cd c8 c9 ca cb cc cd c4 c8 c8 80 27*0 c4 c0 c0 18*c4 5*cd c4 c4 c2 5*c4 5*cd 6*c8 6*c9 6*ca
  //   6*cb 6*ce 6*cc 7*cd c2 c4 11*c2 10*c0 c4 cd c4 c4 c4 cd 5*c4 cd c4 cd 7*c4 c0 c4 c0 c4 c4 c0 c0 c8
  //   c9 ca cb cc cd c4 c8 c9 ca cb cc cd c4 c8 c9 ca cb cc cd c4 c8 c9 ca cb cc cd c4 c8 c9 ca cb cc cd
  //   c4 c8 c9 ca cb cc cd c4 c8 c9 ca cb cc cd c4 c8 c9 ca cb cc cd c4 c8 c9 ca cb cc cd c8 c9 ca cb cc
  //   cd c8 c9 ca cb cc cd c8 c9 ca cb cc cd c8 c9 ca cb cc cd c8 c9 ca cb cc cd c4 c8 c8 80 27*0 c4 c0 c0
  //   18*c4 5*cd c4 c4 c2 5*c4 5*cd 6*c8 6*c9 6*ca 6*cb 6*ce 6*cc 7*cd c2 c4 11*c2 10*c0 c4 c4 c4 cd c4 c4
  //   c4 cd c4 cd c4 c4 c4 cd 8*c4 c0 c4 c0 c0 c4 c0 c8 c9 ca cb cc cd c4 c8 c9 ca cb cc cd c4 c8 c9 ca cb
  //   cc cd c4 c8 c9 ca cb cc cd c4 c8 c9 ca cb cc cd c4 c8 c9 ca cb cc cd c4 c8 c9 ca cb cc cd c4 c8 c9
  //   ca cb cc cd c4 c8 c9 ca cb cc cd c8 c9 ca cb cc cd c8 c9 ca cb cc cd c8 c9 ca cb cc cd c8 c9 ca cb
  //   cc cd c8 c9 ca cb cc cd c4 c8 c8 80 27*0 c4 c0 c0 18*c4 5*cd c4 c4 c2 5*c4 5*cd 6*c8 6*c9 6*ca 6*cb
  //   6*ce 6*cc 7*cd c2 c4 11*c2 10*c0 c4 c4 c4 cd c4 c4 c4 cd c4 c4 c4 cd c4 cd 8*c4 c0 c4 c0 c4 c0 c0 c8
  //   c9 ca cb cc cd c4 c8 c9 ca cb cc cd c4 c8 c9 ca cb cc cd c4 c8 c9 ca cb cc cd c4 c8 c9 ca cb cc cd
  //   c4 c8 c9 ca cb cc cd c4 c8 c9 ca cb cc cd c4 c8 c9 ca cb cc cd c4 c8 c9 ca cb cc cd c8 c9 ca cb cc
  //   cd c8 c9 ca cb cc cd c8 c9 ca cb cc cd c8 c9 ca cb cc cd c8 c9 ca cb cc cd c4 c8 c8 80 27*0 c4 c0 c0
  //   18*c4 5*cd c4 c4 c2 5*c4 5*cd 6*c8 6*c9 6*ca 6*cb 6*ce 6*cc 7*cd c2 c4 11*c2 10*c0 c4 c4 c4 cd c4 cd
  //   c4 c4 c4 cd c4 c4 c4 cd 8*c4 c0 c0 c4 c0 c4 c0 c8 c9 ca cb cc cd c4 c8 c9 ca cb cc cd c4 c8 c9 ca cb
  //   cc cd c4 c8 c9 ca cb cc cd c4 c8 c9 ca cb cc cd c4 c8 c9 ca cb cc cd c4 c8 c9 ca cb cc cd c4 c8 c9
  //   ca cb cc cd c4 c8 c9 ca cb cc cd c8 c9 ca cb cc cd c8 c9 ca cb cc cd c8 c9 ca cb cc cd c8 c9 ca cb
  //   cc cd c8 c9 ca cb cc cd c4 c8 c8 80 27*0 c4 c0 c0 18*c4 5*cd c4 c4 c2 5*c4 5*cd 6*c8 6*c9 6*ca 6*cb
  //   6*ce 6*cc 7*cd c2 c4 11*c2 10*c0 c4 c4 c4 cd c4 cd 5*c4 cd c4 cd 8*c4 c0 c0 c4 c4 c0 c0 c8 c9 ca cb
  //   cc cd c4 c8 c9 ca cb cc cd c4 c8 c9 ca cb cc cd c4 c8 c9 ca cb cc cd c4 c8 c9 ca cb cc cd c4 c8 c9
  //   ca cb cc cd c4 c8 c9 ca cb cc cd c4 c8 c9 ca cb cc cd c4 c8 c9 ca cb cc cd c8 c9 ca cb cc cd c8 c9
  //   ca cb cc cd c8 c9 ca cb cc cd c8 c9 ca cb cc cd c8 c9 ca cb cc cd c4 c8 c8 80 27*0 c5 c4 c4 18*c5
  //   5*cc c5 c5 c3 5*c5 5*cc 42*c4 cc c3 c5 11*c3 10*c2 c5 cc 5*c5 cc c5 cc c5 c5 c5 cc 7*c5 c2 c5 c5 c2
  //   c2 c5 c2 6*d0 c5 6*d0 c5 6*d0 c5 6*d0 c5 6*d0 c5 6*d0 c5 6*d0 c5 6*d0 c5 36*d0 c5 c4 c4 28*0 c5 c4
  //   c4 18*c5 5*cc c5 c5 c3 5*c5 5*cc 42*c4 cc c3 c5 11*c3 10*c2 c5 cc 5*c5 cc c5 c5 c5 cc c5 cc 7*c5 c2
  //   c5 c5 c2 c5 c2 c2 6*d0 c5 6*d0 c5 6*d0 c5 6*d0 c5 6*d0 c5 6*d0 c5 6*d0 c5 6*d0 c5 36*d0 c5 c4 c4
  //   28*0 c5 c4 c4 18*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
  //   contents of rom_3 (hex, n*v repeats v):
  //   95*30 10*10 21*30 10 30 30 10 10 30 10 93*30 70 b0 30 27*0 95*30 10*10 21*30 10 30 30 10 30 10 10
  //   93*30 70 b0 30 27*0 95*30 10*10 21*30 10 30 10 30 10 30 10 93*30 70 b0 30 27*0 95*30 10*10 21*30 10
  //   30 10 30 30 10 10 93*30 70 b0 30 27*0 95*30 10*10 22*30 10 30 10 10 30 10 93*30 70 b0 30 27*0 95*30
  //   10*10 22*30 10 30 10 30 10 10 93*30 70 b0 30 27*0 95*30 10*10 22*30 10 10 30 10 30 10 93*30 70 b0 30
  //   27*0 95*30 10*10 22*30 10 10 30 30 10 10 93*30 70 b0 30 27*0 133*30 6*39 30 6*36 30 6*34 8*30 6*36
  //   30 6*31 30 6*39 30 6*3f 7*30 6*3f 6*30 6*3f 6*30 6*36 30 30 30 28*0 133*30 6*39 30 6*36 30 6*34 8*30
  //   6*36 30 6*31 30 6*39 30 6*3f 7*30 6*3f 6*30 6*3f 6*30 6*36 30 30 30 28*0 133*30 6*39 30 6*36 30 6*34
  //   8*30 6*36 30 6*31 30 6*39 30 6*3f 7*30 6*3f 6*30 6*3f 6*30 6*36 30 30 30 28*0 133*30 6*39 30 6*36 30
  //   6*34 8*30 6*36 30 6*31 30 6*39 30 6*3f 7*30 6*3f 6*30 6*3f 6*30 6*36 30 30 30 28*0 133*30 6*39 30
  //   6*36 30 6*34 8*30 6*36 30 6*31 30 6*39 30 6*3f 7*30 6*3f 6*30 6*3f 6*30 6*36 30 30 30 28*0 133*30
  //   6*39 30 6*36 30 6*34 8*30 6*36 30 6*31 30 6*39 30 6*3f 7*30 6*3f 6*30 6*3f 6*30 6*36 30 30 30 28*0
  //   133*30 6*39 30 6*36 30 6*34 8*30 6*36 30 6*31 30 6*39 30 6*3f 7*30 6*3f 6*30 6*3f 6*30 6*36 30 30 30
  //   28*0 133*30 6*39 30 6*36 30 6*34 8*30 6*36 30 6*31 30 6*39 30 6*3f 7*30 6*3f 6*30 6*3f 6*30 6*36 30
  //   30 30 28*0 28*30 20 55*30 11*20 133*30 28*0 28*30 20 55*30 11*20 133*30 28*0 28*30 20 55*30 11*20
  //   133*30 28*0 28*30 20 55*30 11*20 133*30 28*0 28*30 20 55*30 11*20 133*30 28*0 28*30 20 55*30 11*20
  //   133*30 28*0 28*30 20 55*30 11*20 133*30 28*0 28*30 20 55*30 11*20 133*30 29*0 27*30 20 62*30 4*20
  //   10*10 30 30 4*0 4*30 0 0 30 30 30 0 0 30 30 0 30 10 0 0 10 10 0 10 6*30 39 6*30 36 6*30 34 13*30 36
  //   6*30 31 6*30 39 6*30 3f 36*30 36 30 30 29*0 27*30 20 62*30 4*20 10*10 30 30 4*0 30 30 0 0 5*30 0 0
  //   30 0 30 30 10 0 0 10 0 10 10 6*30 39 6*30 36 6*30 34 13*30 36 6*30 31 6*30 39 6*30 3f 36*30 36 30 30
  //   29*0 27*30 20 62*30 4*20 10*10 30 30 0 0 30 30 0 0 30 30 0 0 30 30 30 0 30 0 30 0 30 10 0 10 0 10 0
  //   10 6*30 39 6*30 36 6*30 34 13*30 36 6*30 31 6*30 39 6*30 3f 36*30 36 30 30 29*0 27*30 20 62*30 4*20
  //   10*10 30 30 0 0 30 30 4*0 5*30 0 30 0 0 30 30 10 0 10 0 0 10 10 6*30 39 6*30 36 6*30 34 13*30 36
  //   6*30 31 6*30 39 6*30 3f 36*30 36 30 30 29*0 27*30 20 62*30 4*20 10*10 0 0 30 30 0 0 4*30 0 0 30 30 0
  //   30 0 30 30 0 30 0 10 0 10 10 0 10 6*30 39 6*30 36 6*30 34 13*30 36 6*30 31 6*30 39 6*30 3f 36*30 36
  //   30 30 29*0 27*30 20 62*30 4*20 10*10 0 0 30 30 0 0 30 30 0 0 4*30 0 30 0 30 0 30 30 0 10 0 10 0 10
  //   10 6*30 39 6*30 36 6*30 34 13*30 36 6*30 31 6*30 39 6*30 3f 36*30 36 30 30 29*0 27*30 20 62*30 4*20
  //   10*10 0 0 4*30 0 0 30 30 0 0 30 30 0 30 30 0 30 0 30 0 10 10 0 10 0 10 6*30 39 6*30 36 6*30 34 13*30
  //   36 6*30 31 6*30 39 6*30 3f 36*30 36 30 30 29*0 27*30 20 62*30 4*20 10*10 0 0 4*30 4*0 4*30 0 30 30 0
  //   0 30 30 0 10 10 0 0 10 10 6*30 39 6*30 36 6*30 34 13*30 36 6*30 31 6*30 39 6*30 3f 36*30 36 30 30
  //   31*0 36*30 42*0 26*30 4*0 4*30 0 0 30 30 30 0 0 30 30 0 30 30 0 0 30 30 0 94*30 33*0 36*30 42*0
  //   26*30 4*0 30 30 0 0 5*30 0 0 30 0 30 30 30 0 0 30 0 95*30 33*0 36*30 42*0 26*30 0 0 30 30 0 0 30 30
  //   0 0 30 30 30 0 30 0 30 0 30 30 0 30 0 30 0 94*30 33*0 36*30 42*0 26*30 0 0 30 30 4*0 5*30 0 30 0 0
  //   30 30 30 0 30 0 0 95*30 33*0 36*30 42*0 24*30 0 0 30 30 0 0 4*30 0 0 30 30 0 30 0 30 30 0 30 0 30 0
  //   30 30 0 94*30 33*0 36*30 42*0 24*30 0 0 30 30 0 0 30 30 0 0 4*30 0 30 0 30 0 30 30 0 30 0 30 0 95*30
  //   33*0 36*30 42*0 24*30 0 0 4*30 0 0 30 30 0 0 30 30 0 30 30 0 30 0 30 0 30 30 0 30 0 94*30 33*0 36*30
  //   42*0 24*30 0 0 4*30 4*0 4*30 0 30 30 0 0 30 30 0 30 30 0 0 95*30 33*0 36*30 45*0 22*30 5*0 30 0 30 0
  //   0 0 30 0 30 0 0 30 30 0 30 30 0 0 30 30 0 30 6*0 30 6*0 30 6*0 30 6*0 30 6*0 30 6*0 30 6*0 30 6*0 30
  //   36*0 30 33*0 36*30 45*0 22*30 5*0 30 0 0 0 30 0 30 0 30 0 0 30 0 30 30 30 0 0 30 0 30 30 6*0 30 6*0
  //   30 6*0 30 6*0 30 6*0 30 6*0 30 6*0 30 6*0 30 36*0 30 33*0 36*30 45*0 22*30 0 0 0 30 0 0 0 30 0 0 0
  //   30 0 30 0 30 0 30 0 30 30 0 30 0 30 0 30 6*0 30 6*0 30 6*0 30 6*0 30 6*0 30 6*0 30 6*0 30 6*0 30
  //   36*0 30 33*0 36*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
  //   contents of rom_4 (hex, n*v repeats v):
  //   c d e 226*c 27*0 c d e 226*c 27*0 c d e 226*c 27*0 c d e 226*c 27*0 c d e 226*c 27*0 c d e 226*c
  //   27*0 c d e 226*c 27*0 c d e 226*c 27*0 228*c 28*0 228*c 28*0 228*c 28*0 228*c 28*0 228*c 28*0 228*c
  //   28*0 228*c 28*0 228*c 28*0 c c c 18*4 5*c 4 4 8 5*4 50*c 11*8 10*c 4 5*c 4 c 4 c c c 4 c 4 c c 4 4 c
  //   4 13*c 4 6*c 4 6*c 4 6*c 4 6*c 4 6*c 4 6*c 4 6*c 4 36*c 4 c c 28*0 c c c 18*4 5*c 4 4 8 5*4 50*c
  //   11*8 10*c 4 5*c 4 c c c 4 c 4 c 4 c c 4 c 4 4 13*c 4 6*c 4 6*c 4 6*c 4 6*c 4 6*c 4 6*c 4 6*c 4 36*c
  //   4 c c 28*0 c c c 18*4 5*c 4 4 8 5*4 50*c 11*8 10*c 4 c c c 4 c c c 4 c c c 4 c 4 c 4 c 4 c 4 13*c 4
  //   6*c 4 6*c 4 6*c 4 6*c 4 6*c 4 6*c 4 6*c 4 36*c 4 c c 28*0 c c c 18*4 5*c 4 4 8 5*4 50*c 11*8 10*c 4
  //   c c c 4 5*c 4 c 4 c 4 c 4 c c 4 4 13*c 4 6*c 4 6*c 4 6*c 4 6*c 4 6*c 4 6*c 4 6*c 4 36*c 4 c c 28*0 c
  //   c c 18*4 5*c 4 4 8 5*4 50*c 11*8 12*c 4 c c c 4 c 4 c c c 4 c c 4 c 4 4 c 4 13*c 4 6*c 4 6*c 4 6*c 4
  //   6*c 4 6*c 4 6*c 4 6*c 4 36*c 4 c c 28*0 c c c 18*4 5*c 4 4 8 5*4 50*c 11*8 12*c 4 c c c 4 c c c 4 c
  //   4 c c 4 c 4 c 4 4 13*c 4 6*c 4 6*c 4 6*c 4 6*c 4 6*c 4 6*c 4 6*c 4 36*c 4 c c 28*0 c c c 18*4 5*c 4
  //   4 8 5*4 50*c 11*8 12*c 4 c 4 c c c 4 c c c 4 c c 4 4 c 4 c 4 13*c 4 6*c 4 6*c 4 6*c 4 6*c 4 6*c 4
  //   6*c 4 6*c 4 36*c 4 c c 28*0 c c c 18*4 5*c 4 4 8 5*4 50*c 11*8 12*c 4 c 4 5*c 4 c 4 c c 4 4 c c 4 4
  //   13*c 4 6*c 4 6*c 4 6*c 4 6*c 4 6*c 4 6*c 4 6*c 4 36*c 4 c c 29*0 94*c 10*4 c c 4*0 4*c 0 0 c c c 0 0
  //   c c 0 c 4 0 0 4 4 0 4 95*c 29*0 94*c 10*4 c c 4*0 c c 0 0 5*c 0 0 c 0 c c 4 0 0 4 0 4 4 95*c 29*0
  //   94*c 10*4 c c 0 0 c c 0 0 c c 0 0 c c c 0 c 0 c 0 c 4 0 4 0 4 0 4 95*c 29*0 94*c 10*4 c c 0 0 c c
  //   4*0 5*c 0 c 0 0 c c 4 0 4 0 0 4 4 95*c 29*0 94*c 10*4 0 0 c c 0 0 4*c 0 0 c c 0 c 0 c c 0 c 0 4 0 4
  //   4 0 4 95*c 29*0 94*c 10*4 0 0 c c 0 0 c c 0 0 4*c 0 c 0 c 0 c c 0 4 0 4 0 4 4 95*c 29*0 94*c 10*4 0
  //   0 4*c 0 0 c c 0 0 c c 0 c c 0 c 0 c 0 4 4 0 4 0 4 95*c 29*0 94*c 10*4 0 0 4*c 4*0 4*c 0 c c 0 0 c c
  //   0 4 4 0 0 4 4 95*c 31*0 36*c 42*0 26*c 4*0 4*c 0 0 c c c 0 0 c c 0 c c 0 0 c c 0 94*c 33*0 36*c 42*0
  //   26*c 4*0 c c 0 0 5*c 0 0 c 0 c c c 0 0 c 0 95*c 33*0 36*c 42*0 26*c 0 0 c c 0 0 c c 0 0 c c c 0 c 0
  //   c 0 c c 0 c 0 c 0 94*c 33*0 36*c 42*0 26*c 0 0 c c 4*0 5*c 0 c 0 0 c c c 0 c 0 0 95*c 33*0 36*c 42*0
  //   24*c 0 0 c c 0 0 4*c 0 0 c c 0 c 0 c c 0 c 0 c 0 c c 0 94*c 33*0 36*c 42*0 24*c 0 0 c c 0 0 c c 0 0
  //   4*c 0 c 0 c 0 c c 0 c 0 c 0 95*c 33*0 36*c 42*0 24*c 0 0 4*c 0 0 c c 0 0 c c 0 c c 0 c 0 c 0 c c 0 c
  //   0 94*c 33*0 36*c 42*0 24*c 0 0 4*c 4*0 4*c 0 c c 0 0 c c 0 c c 0 0 95*c 33*0 36*c 45*0 22*c 5*0 c 0
  //   c 0 0 0 c 0 c 0 0 c c 0 c c 0 0 c c 0 c 6*0 c 6*0 c 6*0 c 6*0 c 6*0 c 6*0 c 6*0 c 6*0 c 36*0 c 33*0
  //   36*c 45*0 22*c 5*0 c 0 0 0 c 0 c 0 c 0 0 c 0 c c c 0 0 c 0 c c 6*0 c 6*0 c 6*0 c 6*0 c 6*0 c 6*0 c
  //   6*0 c 6*0 c 36*0 c 33*0 36*c 45*0 22*c 0 0 0 c 0 0 0 c 0 0 0 c 0 c 0 c 0 c 0 c c 0 c 0 c 0 c 6*0 c
  //   6*0 c 6*0 c 6*0 c 6*0 c 6*0 c 6*0 c 6*0 c 36*0 c 33*0 36*c 45*0 22*c 0 0 0 c 5*0 c 0 c 0 c 0 c 0 0 c
  //   c c 0 c 0 0 c c 6*0 c 6*0 c 6*0 c 6*0 c 6*0 c 6*0 c 6*0 c 6*0 c 36*0 c 33*0 36*c 45*0 21*c 0 0 c 0 0
  //   0 c 0 c 0 0 0 c 0 0 c 0 c c 0 c 0 c 0 c c 0 c 6*0 c 6*0 c 6*0 c 6*0 c 6*0 c 6*0 c 6*0 c 6*0 c 36*0 c
  //   33*0 36*c 45*0 21*c 0 0 c 0 0 0 c 0 0 0 c 0 c 0 0 c 0 c 0 c c 0 c 0 c 0 c c 6*0 c 6*0 c 6*0 c 6*0 c
  //   6*0 c 6*0 c 6*0 c 6*0 c 36*0 c 33*0 36*c 45*0 21*c 0 0 c 0 c 0 0 0 c 0 0 0 c 0 0 c c 0 c 0 c 0 c c 0
  //   c 0 c 6*0 c 6*0 c 6*0 c 6*0 c 6*0 c 6*0 c 6*0 c 6*0 c 36*0 c 33*0 36*c 45*0 21*c 0 0 c 0 c 5*0 c 0 c
  //   0 0 c c 0 0 c c 0 c c 0 0 c c 6*0 c 6*0 c 6*0 c 6*0 c 6*0 c 6*0 c 6*0 c 6*0 c 36*0 c 34*0 c 0 c 0 c
  //   0 c 0 c 0 c 0 5*c 5*0 8*c 57*0 15*c 5*0 c 0 c 0 0 0 c 0 8 0 0 8 8 0 8 c 0 0 c c 0 c 6*0 c 6*0 c 6*0
  //   c 6*0 c 6*0 c 6*0 c 6*0 c 6*0 c 36*0 c 34*0 c 0 c 0 c 0 c 0 c 0 c 0 5*c 5*0 8*c 57*0 15*c 5*0 c 0 0
  //   0 c 0 c 0 8 0 0 8 0 8 8 c 0 0 c 0 c c 6*0 c 6*0 c 6*0 c 6*0 c 6*0 c 6*0 c 6*0 c 6*0 c 36*0 c 34*0 c
  //   0 c 0 c 0 c 0 c 0 c 0 5*c 5*0 8*c 57*0 15*c 0 0 0 c 0 0 0 c 0 0 0 c 0 8 0 8 0 8 0 8 c 0 c 0 c 0 c
  //   6*0 c 6*0 c 6*0 c 6*0 c 6*0 c 6*0 c 6*0 c 6*0 c 36*0 c 34*0 c 0 c 0 c 0 c 0 c 0 c 0 5*c 5*0 8*c 57*0
  //   15*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
endmodule

module StepCounter (
  input  Clk,
  input  NotReset,
  input  Clear,
  input  NotHalt,
  input  NotWait,
  output [3:0] Step
);

  wire and_1_out, n74161_1_pin3, n74161_1_pin4, n74161_1_pin5, n74161_1_pin6, n74161_1_pin10, not_1_out;

  not not_1 (not_1_out, Clear);
  and and_1 (and_1_out, NotHalt, NotWait);
  _74161 u_74161_1 (
    .pin1(NotReset), .pin2(Clk), .pin3(n74161_1_pin3), .pin4(n74161_1_pin4), .pin5(n74161_1_pin5),
    .pin6(n74161_1_pin6), .pin7(and_1_out), .pin14(Step[0]), .pin13(Step[1]), .pin12(Step[2]),
    .pin11(Step[3]), .pin10(n74161_1_pin10), .pin9(not_1_out));  // open: pin15
  // also tied to GND on the sheet: {n74161_1_pin3, n74161_1_pin4, n74161_1_pin5, n74161_1_pin6}
  // also tied to VCC on the sheet: n74161_1_pin10
endmodule

module ProgramCounter (
  input  NotReset,
  input  HFromD,
  input  Clk,
  input  HToD,
  input  [7:0] DIn,
  input  LFromD,
  input  NotInc,
  input  LToD,
  output [7:0] DOut
);

  wire and_1_out, counter_2_carry, not_1_out, not_2_out;
  wire [3:0] counter_1_q, counter_1_q_2, counter_2_q, counter_2_q_2;

  not not_1 (not_1_out, NotReset);
  not not_2 (not_2_out, NotInc);
  Counter counter_1 (
    .clr(not_1_out), .load(HFromD), .up(not_2_out), .count(and_1_out), .clk(Clk), .D(DIn),
    .Q({counter_1_q_2, counter_1_q}));  // open: carry
  and and_1 (and_1_out, not_2_out, counter_2_carry);
  Counter counter_2 (
    .clr(not_1_out), .load(LFromD), .up(not_2_out), .count(not_2_out), .clk(Clk), .D(DIn),
    .carry(counter_2_carry), .Q({counter_2_q_2, counter_2_q}));
  assign DOut = HToD ? {counter_1_q_2, counter_1_q} : 8'bz;  // Controlled_Buffer controlled_buffer_1
  assign DOut = LToD ? {counter_2_q_2, counter_2_q} : 8'bz;  // Controlled_Buffer controlled_buffer_2
  Hex_Digit_Display hex_digit_display_1 (.value(counter_1_q_2));  // open: dp
  Hex_Digit_Display hex_digit_display_2 (.value(counter_1_q));  // open: dp
  Hex_Digit_Display hex_digit_display_3 (.value(counter_2_q_2));  // open: dp
  Hex_Digit_Display hex_digit_display_4 (.value(counter_2_q));  // open: dp
endmodule

module AddressRegister (
  input  NotReset,
  input  HFromD,
  input  Clk,
  input  [7:0] DIn,
  input  LFromD,
  input  NotInc,
  input  NotDec,
  output [15:0] Address
);

  wire and_1_out, counter_2_carry, not_1_out, not_2_out, not_3_out, or_1_out;

  not not_1 (not_1_out, NotReset);
  not not_2 (not_2_out, NotInc);
  not not_3 (not_3_out, NotDec);
  or or_1 (or_1_out, not_2_out, not_3_out);
  Counter counter_1 (
    .clr(not_1_out), .load(HFromD), .up(not_2_out), .count(and_1_out), .clk(Clk), .D(DIn), .Q(Address[15:8]));  // open: carry
  and and_1 (and_1_out, or_1_out, counter_2_carry);
  Counter counter_2 (
    .clr(not_1_out), .load(LFromD), .up(not_2_out), .count(or_1_out), .clk(Clk), .D(DIn),
    .carry(counter_2_carry), .Q(Address[7:0]));
  Hex_Digit_Display hex_digit_display_1 (.value(Address[15:12]));  // open: dp
  Hex_Digit_Display hex_digit_display_2 (.value(Address[11:8]));  // open: dp
  Hex_Digit_Display hex_digit_display_3 (.value(Address[7:4]));  // open: dp
  Hex_Digit_Display hex_digit_display_4 (.value(Address[3:0]));  // open: dp
endmodule
